# Fritzing sketch Mood (saved by Fritzing 0.9.1b)
breadboards: 1

parts:
  Part1 = Arduino Uno (Rev3)
  LED1 = RGB LED (com. cathode, rgb) [package="5 mm [THT]"]
  R1 = Resistor [tolerance=±5% resistance=220 power=330 package=THT]
  R2 = Resistor [tolerance=±5% resistance=220 power=330 package=THT]
  R3 = Resistor [tolerance=±5% resistance=220 power=330 package=THT]
  T1 = LM35 Temperature Sensor [package="TO92 [THT]"]

nets:
  N1: Part1.A0, T1.Vout
  N2: Part1.D9_PWM, R3.Pin_0
  N3: Part1.D10_PWM/SS, R1.Pin_0
  N4: Part1.D11_PWM/MOSI, R2.Pin_0
  GND: Part1.GND, LED1.common_cathode, T1.GND
  N5: Part1.5V, T1.+Vs
  N6: LED1.red_anode, R3.Pin_1
  N7: LED1.green_anode, R1.Pin_1
  N8: LED1.blue_anode, R2.Pin_1

// code stored in the sketch: Mood.ino
 /*****************************************************
    MOOD LIGHTING
    This sketch reads in a temperature value
    from a TMP36 sensor and uses it to set the
    color of an RGB LED. The LED only responds to
    a range of temperatures from about 16-27 C
    (~60-80 F). Every 1 C (~2 F) temp change will
    shift the mood light to a new color.
    ***************************************************/
  
  //Initialize pins for temperature sensor and RBG LED
  int tempPin = A0;
  int r = 9;
  int g = 10;
  int b = 11;
  
  //Set colors for mood light to cycle through
  int rRange[] = {255,255,127,0,0,0,0,0,127,255,255,255};
  int bRange[] = {0,0,0,0,127,255,255,255,255,255,127,0};
  int gRange[] = {127,255,255,255,255,255,127,0,0,0,0,0};
  
  void setup() {
    Serial.begin(9600);
    pinMode(r, OUTPUT);
    pinMode(g, OUTPUT);
    pinMode(b, OUTPUT);
  }    
  
  void loop() {
    int val = analogRead(tempPin);
    int color = val;
    
    // 147 mV = 22 C, 72 F (approx room temp)
    // +1 C = + 1.8 F = +10 mV
    // If we change color every 10 mV, we need
    // to use the range from 87-197 mV
    if(val < 87) color = 87;
    else if (val > 197) color = 197;
    color = (color-87)/12;
  
    analogWrite(r,rRange[color]);
    analogWrite(g,gRange[color]);
    analogWrite(b,bRange[color]);
    
    // Convert voltage reading to temperature
    // Reading will give a value b/n 0 and 1023
    // 0.5V = 25 C; each 0.1V = 1 C
    float volts = (val * 5.0) / 1024.0;
    float tempC = (volts-0.5) * 100;
    float tempF = tempC * 1.8 + 32;
    // Print out temp in Fahrenheit
    Serial.println(tempF);
    delay(500);
  }
