# Fritzing sketch Scroll (saved by Fritzing 0.9.1b)
breadboards: 1

parts:
  Part3 = Arduino Uno (Rev3)
  R8 = Rotary Potentiometer (Small) [maximum_resistance=100kΩ package=THT]
  LCD2 = LCD screen

nets:
  N1: Part3.D11_PWM/MOSI, LCD2.E
  N2: Part3.D12/MISO, LCD2.RS
  GND: Part3.GND, R8.leg1, LCD2.VSS, LCD2.R/W
  N3: Part3.D2, LCD2.LED-
  N4: Part3.D3_PWM, LCD2.LED+
  N5: Part3.D4, LCD2.DB7
  N6: Part3.D5_PWM, LCD2.DB6
  5V: Part3.5V, R8.leg2, LCD2.VDD
  N7: R8.wiper, LCD2.V0
